// Logisim project nand2tetris_proj_01.circ as structural Verilog: 16 circuits, main circuit Not
module Not (
  input  in,
  output out
);

  nand nand_1 (out, in, in);

  // Notes on the sheet:
  //   Chaper 1: Not
endmodule

module And (
  input  a,
  input  b,
  output out
);

  wire nand_1_out;

  nand nand_1 (nand_1_out, a, b);
  nand nand_2 (out, nand_1_out, nand_1_out);

  // Notes on the sheet:
  //   Chapter 1: And
endmodule

module Or (
  input  a,
  input  b,
  output out
);

  wire nand_1_out, nand_2_out;

  nand nand_1 (nand_1_out, a, a);
  nand nand_2 (nand_2_out, b, b);
  nand nand_3 (out, nand_1_out, nand_2_out);

  // Notes on the sheet:
  //   Chapter 1: Or
endmodule

module Xor (
  input  a,
  input  b,
  output out
);

  wire and_1_out, and_2_out, not_1_out, not_2_out;

  not not_1 (not_1_out, b);
  not not_2 (not_2_out, a);
  and and_1 (and_1_out, a, not_1_out);
  and and_2 (and_2_out, not_2_out, b);
  or or_1 (out, and_1_out, and_2_out);

  // Notes on the sheet:
  //   Chapter 1: Xor
endmodule

module Mux (
  input  a,
  input  b,
  input  sel,
  output out
);

  wire and_1_out, and_2_out, not_1_out;

  not not_1 (not_1_out, sel);
  and and_1 (and_1_out, a, not_1_out);
  and and_2 (and_2_out, sel, b);
  or or_1 (out, and_1_out, and_2_out);

  // Notes on the sheet:
  //   Chapter 1: Mux
endmodule

module Demux (
  input  in,
  input  sel,
  output a,
  output b
);

  wire not_1_out;

  not not_1 (not_1_out, sel);
  and and_1 (a, in, not_1_out);
  and and_2 (b, in, sel);

  // Notes on the sheet:
  //   Chapter 1: Demux
endmodule

module And16 (
  input  a0,
  input  a8,
  input  b0,
  input  b8,
  input  a1,
  input  a9,
  input  b1,
  input  b9,
  input  a2,
  input  a10,
  input  b2,
  input  b10,
  input  a3,
  input  a11,
  input  b3,
  input  b11,
  input  a4,
  input  a12,
  input  b4,
  input  b12,
  input  a5,
  input  a13,
  input  b5,
  input  b13,
  input  a6,
  input  a14,
  input  b6,
  input  b14,
  input  a7,
  input  a15,
  input  b7,
  input  b15,
  output out0,
  output out8,
  output out1,
  output out9,
  output out2,
  output out10,
  output out3,
  output out11,
  output out4,
  output out12,
  output out5,
  output out13,
  output out6,
  output out14,
  output out7,
  output out15
);

  and and_1 (out0, a0, b0);
  and and_2 (out1, a1, b1);
  and and_3 (out2, a2, b2);
  and and_4 (out3, a3, b3);
  and and_5 (out4, a4, b4);
  and and_6 (out5, a5, b5);
  and and_7 (out6, a6, b6);
  and and_8 (out7, a7, b7);
  and and_9 (out8, a8, b8);
  and and_10 (out9, a9, b9);
  and and_11 (out10, a10, b10);
  and and_12 (out11, a11, b11);
  and and_13 (out12, a12, b12);
  and and_14 (out13, a13, b13);
  and and_15 (out14, a14, b14);
  and and_16 (out15, a15, b15);

  // Notes on the sheet:
  //   Chapter 1: And16
endmodule

module Not16 (
  input  in0,
  input  in1,
  input  in2,
  input  in3,
  input  in4,
  input  in5,
  input  in6,
  input  in7,
  input  in8,
  input  in9,
  input  in10,
  input  in11,
  input  in12,
  input  in13,
  input  in14,
  input  in15,
  output out0,
  output out1,
  output out2,
  output out3,
  output out4,
  output out5,
  output out6,
  output out7,
  output out8,
  output out9,
  output out10,
  output out11,
  output out12,
  output out13,
  output out14,
  output out15
);

  not not_1 (out0, in0);
  not not_2 (out1, in1);
  not not_3 (out2, in2);
  not not_4 (out3, in3);
  not not_5 (out4, in4);
  not not_6 (out5, in5);
  not not_7 (out6, in6);
  not not_8 (out7, in7);
  not not_9 (out8, in8);
  not not_10 (out9, in9);
  not not_11 (out10, in10);
  not not_12 (out11, in11);
  not not_13 (out12, in12);
  not not_14 (out13, in13);
  not not_15 (out14, in14);
  not not_16 (out15, in15);

  // Notes on the sheet:
  //   Chapter 1: Not16
endmodule

module Or16 (
  input  a0,
  input  a8,
  input  b0,
  input  b8,
  input  a1,
  input  a9,
  input  b1,
  input  b9,
  input  a2,
  input  a10,
  input  b2,
  input  b10,
  input  a3,
  input  a11,
  input  b3,
  input  b11,
  input  a4,
  input  a12,
  input  b4,
  input  b12,
  input  a5,
  input  a13,
  input  b5,
  input  b13,
  input  a6,
  input  a14,
  input  b6,
  input  b14,
  input  a7,
  input  a15,
  input  b7,
  input  b15,
  output out0,
  output out8,
  output out1,
  output out9,
  output out2,
  output out10,
  output out3,
  output out11,
  output out4,
  output out12,
  output out5,
  output out13,
  output out6,
  output out14,
  output out7,
  output out15
);

  or or_1 (out0, a0, b0);
  or or_2 (out1, a1, b1);
  or or_3 (out2, a2, b2);
  or or_4 (out3, a3, b3);
  or or_5 (out4, a4, b4);
  or or_6 (out5, a5, b5);
  or or_7 (out6, a6, b6);
  or or_8 (out7, a7, b7);
  or or_9 (out8, a8, b8);
  or or_10 (out9, a9, b9);
  or or_11 (out10, a10, b10);
  or or_12 (out11, a11, b11);
  or or_13 (out12, a12, b12);
  or or_14 (out13, a13, b13);
  or or_15 (out14, a14, b14);
  or or_16 (out15, a15, b15);

  // Notes on the sheet:
  //   Chapter 1: Or16
endmodule

module Mux16 (
  input  [15:0] a,
  input  [15:0] b,
  input  sel,
  output [15:0] out_4
);

  Mux mux_1 (.a(a[0]), .b(b[0]), .out(out_4[0]), .sel(sel));
  Mux mux_2 (.a(a[1]), .b(b[1]), .out(out_4[1]), .sel(sel));
  Mux mux_3 (.a(a[2]), .b(b[2]), .out(out_4[2]), .sel(sel));
  Mux mux_4 (.a(a[3]), .b(b[3]), .out(out_4[3]), .sel(sel));
  Mux mux_5 (.a(a[4]), .b(b[4]), .out(out_4[4]), .sel(sel));
  Mux mux_6 (.a(a[5]), .b(b[5]), .out(out_4[5]), .sel(sel));
  Mux mux_7 (.a(a[6]), .b(b[6]), .out(out_4[6]), .sel(sel));
  Mux mux_8 (.a(a[7]), .b(b[7]), .out(out_4[7]), .sel(sel));
  Mux mux_9 (.a(a[8]), .b(b[8]), .out(out_4[8]), .sel(sel));
  Mux mux_10 (.a(a[9]), .b(b[9]), .out(out_4[9]), .sel(sel));
  Mux mux_11 (.a(a[10]), .b(b[10]), .out(out_4[10]), .sel(sel));
  Mux mux_12 (.a(a[11]), .b(b[11]), .out(out_4[11]), .sel(sel));
  Mux mux_13 (.a(a[12]), .b(b[12]), .out(out_4[12]), .sel(sel));
  Mux mux_14 (.a(a[13]), .b(b[13]), .out(out_4[13]), .sel(sel));
  Mux mux_15 (.a(a[14]), .b(b[14]), .out(out_4[14]), .sel(sel));
  Mux mux_16 (.a(a[15]), .b(b[15]), .out(out_4[15]), .sel(sel));

  // Notes on the sheet:
  //   Chapter 1: Mux16
endmodule

module Or8Way (
  input  in0,
  input  in1,
  input  in2,
  input  in3,
  input  in4,
  input  in5,
  input  in6,
  input  in7,
  output out
);

  wire or_1_out, or_2_out, or_3_out, or_4_out, or_5_out, or_6_out;

  or or_1 (or_1_out, in0, in1);
  or or_2 (or_2_out, in2, in3);
  or or_3 (or_3_out, in4, in5);
  or or_4 (or_4_out, in6, in7);
  or or_5 (or_5_out, or_1_out, or_2_out);
  or or_6 (or_6_out, or_3_out, or_4_out);
  or or_7 (out, or_5_out, or_6_out);

  // Notes on the sheet:
  //   Chapter 1: Or8Way
endmodule

module Mux4Way16 (
  input  [15:0] a,
  input  [15:0] b,
  input  [15:0] c,
  input  [15:0] d,
  input  [1:0] sel,
  output [15:0] out
);

  wire [15:0] mux16_1_out_4, mux16_2_out_4;

  Mux16 mux16_1 (.a(a), .b(b), .sel(sel[0]), .out_4(mux16_1_out_4));
  Mux16 mux16_2 (.a(c), .b(d), .sel(sel[0]), .out_4(mux16_2_out_4));
  Mux16 mux16_3 (.a(mux16_1_out_4), .b(mux16_2_out_4), .sel(sel[1]), .out_4(out));

  // Notes on the sheet:
  //   Chapter 1: Mux4Way16
endmodule

module Mux8Way16 (
  input  [15:0] a,
  input  [15:0] b,
  input  [15:0] c,
  input  [15:0] d,
  input  [15:0] e,
  input  [15:0] f,
  input  [15:0] g,
  input  [15:0] h,
  input  [2:0] sel,
  output [15:0] out
);

  wire [15:0] mux4way16_1_out, mux4way16_2_out;

  Mux4Way16 mux4way16_1 (.a(a), .b(b), .c(c), .d(d), .out(mux4way16_1_out), .sel(sel[1:0]));
  Mux4Way16 mux4way16_2 (.a(e), .b(f), .c(g), .d(h), .out(mux4way16_2_out), .sel(sel[1:0]));
  Mux16 mux16_1 (.a(mux4way16_1_out), .b(mux4way16_2_out), .sel(sel[2]), .out_4(out));

  // Notes on the sheet:
  //   Chapter 1: Mux8Way16
endmodule

module DMux4Way (
  input  in,
  input  [1:0] in_2,
  output a,
  output b,
  output c,
  output d
);

  wire demux_1_a, demux_1_b;

  Demux demux_1 (.in(in), .a(demux_1_a), .b(demux_1_b), .sel(in_2[1]));
  Demux demux_2 (.in(demux_1_a), .a(a), .b(b), .sel(in_2[0]));
  Demux demux_3 (.in(demux_1_b), .a(c), .b(d), .sel(in_2[0]));

  // Notes on the sheet:
  //   Chapter 1: DMux4Way
endmodule

module DMux8Way (
  input  in,
  input  [2:0] sel,
  output a,
  output b,
  output c,
  output d,
  output e,
  output f,
  output g,
  output h
);

  wire dmux4way_1_a, dmux4way_1_b, dmux4way_1_c, dmux4way_1_d;

  DMux4Way dmux4way_1 (
    .in(in), .a(dmux4way_1_a), .b(dmux4way_1_b), .c(dmux4way_1_c), .d(dmux4way_1_d), .in_2(sel[2:1]));
  Demux demux_1 (.in(dmux4way_1_a), .a(a), .b(b), .sel(sel[0]));
  Demux demux_2 (.in(dmux4way_1_b), .a(c), .b(d), .sel(sel[0]));
  Demux demux_3 (.in(dmux4way_1_c), .a(e), .b(f), .sel(sel[0]));
  Demux demux_4 (.in(dmux4way_1_d), .a(g), .b(h), .sel(sel[0]));

  // Notes on the sheet:
  //   Chapter 1: DMux8Way
endmodule

module Main (
);

  Or8Way or8way_1 ();  // open: in0, in1, in2, in3, in4, in5, in6, in7, out
  Mux mux_1 ();  // open: a, b, out, sel
  Demux demux_1 ();  // open: in, a, b, sel
  Mux16 mux16_1 ();  // open: a, b, sel, out_4
  DMux4Way dmux4way_1 ();  // open: in, a, b, c, d, in_2
  DMux8Way dmux8way_1 ();  // open: in, sel, a, b, c, d, e, f, g, h
  Mux4Way16 mux4way16_1 ();  // open: a, b, c, d, out, sel
  Mux8Way16 mux8way16_1 ();  // open: a, b, c, d, e, f, g, h, sel, out

  // Notes on the sheet:
  //   Chapter 1: some of the interfaces
endmodule
