// Logisim project nand2tetris_proj_02.circ as structural Verilog: 6 circuits, main circuit HalfAdder
// Half+
module HalfAdder (
  input  a,
  input  b,
  output sum,
  output carry
);

  xor xor_1 (sum, a, b);
  and and_1 (carry, a, b);

  // Notes on the sheet:
  //   Chapter 2: HalfAdder
endmodule

// Full+
module FullAdder (
  input  a,
  input  b,
  input  c,
  output sum,
  output carry
);

  wire halfadder_1_carry, halfadder_1_sum, halfadder_2_carry;

  HalfAdder halfadder_1 (.a(a), .b(b), .sum(halfadder_1_sum), .carry(halfadder_1_carry));
  HalfAdder halfadder_2 (.a(halfadder_1_sum), .b(c), .sum(sum), .carry(halfadder_2_carry));
  or or_1 (carry, halfadder_2_carry, halfadder_1_carry);

  // Notes on the sheet:
  //   Chapter 2: FullAdder
endmodule

module Add16 (
  input  [15:0] a,
  input  [15:0] b,
  output [15:0] out
);

  wire fulladder_1_carry, fulladder_2_carry, fulladder_3_carry, fulladder_4_carry, fulladder_5_carry,
       fulladder_6_carry, fulladder_7_carry, fulladder_8_carry, fulladder_9_carry, fulladder_10_carry,
       fulladder_11_carry, fulladder_12_carry, fulladder_13_carry, fulladder_14_carry, fulladder_15_carry;

  FullAdder fulladder_1 (.a(a[0]), .b(b[0]), .c(1'b0), .sum(out[0]), .carry(fulladder_1_carry));
  FullAdder fulladder_2 (.a(a[1]), .b(b[1]), .c(fulladder_1_carry), .sum(out[1]), .carry(fulladder_2_carry));
  FullAdder fulladder_3 (.a(a[2]), .b(b[2]), .c(fulladder_2_carry), .sum(out[2]), .carry(fulladder_3_carry));
  FullAdder fulladder_4 (.a(a[3]), .b(b[3]), .c(fulladder_3_carry), .sum(out[3]), .carry(fulladder_4_carry));
  FullAdder fulladder_5 (.a(a[4]), .b(b[4]), .c(fulladder_4_carry), .sum(out[4]), .carry(fulladder_5_carry));
  FullAdder fulladder_6 (.a(a[5]), .b(b[5]), .c(fulladder_5_carry), .sum(out[5]), .carry(fulladder_6_carry));
  FullAdder fulladder_7 (.a(a[6]), .b(b[6]), .c(fulladder_6_carry), .sum(out[6]), .carry(fulladder_7_carry));
  FullAdder fulladder_8 (.a(a[7]), .b(b[7]), .c(fulladder_7_carry), .sum(out[7]), .carry(fulladder_8_carry));
  FullAdder fulladder_9 (.a(a[8]), .b(b[8]), .c(fulladder_8_carry), .sum(out[8]), .carry(fulladder_9_carry));
  FullAdder fulladder_10 (.a(a[9]), .b(b[9]), .c(fulladder_9_carry), .sum(out[9]), .carry(fulladder_10_carry));
  FullAdder fulladder_11 (.a(a[10]), .b(b[10]), .c(fulladder_10_carry), .sum(out[10]), .carry(fulladder_11_carry));
  FullAdder fulladder_12 (.a(a[11]), .b(b[11]), .c(fulladder_11_carry), .sum(out[11]), .carry(fulladder_12_carry));
  FullAdder fulladder_13 (.a(a[12]), .b(b[12]), .c(fulladder_12_carry), .sum(out[12]), .carry(fulladder_13_carry));
  FullAdder fulladder_14 (.a(a[13]), .b(b[13]), .c(fulladder_13_carry), .sum(out[13]), .carry(fulladder_14_carry));
  FullAdder fulladder_15 (.a(a[14]), .b(b[14]), .c(fulladder_14_carry), .sum(out[14]), .carry(fulladder_15_carry));
  FullAdder fulladder_16 (.a(a[15]), .b(b[15]), .c(fulladder_15_carry), .sum(out[15]));  // open: carry

  // Notes on the sheet:
  //   Chapter 2: Add16
endmodule

module Inc16 (
  input  [15:0] in,
  output [15:0] out
);

  wire fulladder_1_carry, fulladder_2_carry, fulladder_3_carry, fulladder_4_carry, fulladder_5_carry,
       fulladder_6_carry, fulladder_7_carry, fulladder_8_carry, fulladder_9_carry, fulladder_10_carry,
       fulladder_11_carry, fulladder_12_carry, fulladder_13_carry, fulladder_14_carry, fulladder_15_carry;

  FullAdder fulladder_1 (.a(in[0]), .b(1'b1), .c(1'b0), .sum(out[0]), .carry(fulladder_1_carry));
  FullAdder fulladder_2 (.a(in[1]), .b(1'b0), .c(fulladder_1_carry), .sum(out[1]), .carry(fulladder_2_carry));
  FullAdder fulladder_3 (.a(in[2]), .b(1'b0), .c(fulladder_2_carry), .sum(out[2]), .carry(fulladder_3_carry));
  FullAdder fulladder_4 (.a(in[3]), .b(1'b0), .c(fulladder_3_carry), .sum(out[3]), .carry(fulladder_4_carry));
  FullAdder fulladder_5 (.a(in[4]), .b(1'b0), .c(fulladder_4_carry), .sum(out[4]), .carry(fulladder_5_carry));
  FullAdder fulladder_6 (.a(in[5]), .b(1'b0), .c(fulladder_5_carry), .sum(out[5]), .carry(fulladder_6_carry));
  FullAdder fulladder_7 (.a(in[6]), .b(1'b0), .c(fulladder_6_carry), .sum(out[6]), .carry(fulladder_7_carry));
  FullAdder fulladder_8 (.a(in[7]), .b(1'b0), .c(fulladder_7_carry), .sum(out[7]), .carry(fulladder_8_carry));
  FullAdder fulladder_9 (.a(in[8]), .b(1'b0), .c(fulladder_8_carry), .sum(out[8]), .carry(fulladder_9_carry));
  FullAdder fulladder_10 (.a(in[9]), .b(1'b0), .c(fulladder_9_carry), .sum(out[9]), .carry(fulladder_10_carry));
  FullAdder fulladder_11 (.a(in[10]), .b(1'b0), .c(fulladder_10_carry), .sum(out[10]), .carry(fulladder_11_carry));
  FullAdder fulladder_12 (.a(in[11]), .b(1'b0), .c(fulladder_11_carry), .sum(out[11]), .carry(fulladder_12_carry));
  FullAdder fulladder_13 (.a(in[12]), .b(1'b0), .c(fulladder_12_carry), .sum(out[12]), .carry(fulladder_13_carry));
  FullAdder fulladder_14 (.a(in[13]), .b(1'b0), .c(fulladder_13_carry), .sum(out[13]), .carry(fulladder_14_carry));
  FullAdder fulladder_15 (.a(in[14]), .b(1'b0), .c(fulladder_14_carry), .sum(out[14]), .carry(fulladder_15_carry));
  FullAdder fulladder_16 (.a(in[15]), .b(1'b0), .c(fulladder_15_carry), .sum(out[15]));  // open: carry

  // Notes on the sheet:
  //   Chapter 2: Inc16
endmodule

module ALU (
  input  zx,
  input  nx,
  input  f,
  input  no,
  input  [15:0] x,
  input  [15:0] y,
  input  zy,
  input  ny,
  output [15:0] out,
  output zr,
  output ng
);

  wire or8way_1_out, or8way_2_out, or_1_out;
  wire [15:0] add16_1_out, and_1_out, mux16_1_out_4, mux16_2_out_4, mux16_3_out_4, mux16_4_out_4,
       mux16_5_out_4, not_1_out, not_2_out, not_3_out;

  Mux16 mux16_1 (.a(x), .b({16{1'b0}}), .sel(zx), .out_4(mux16_1_out_4));
  Mux16 mux16_2 (.a(y), .b({16{1'b0}}), .sel(zy), .out_4(mux16_2_out_4));
  assign not_1_out = ~mux16_1_out_4;  // NOT_Gate not_1, 16 bits wide
  assign not_2_out = ~mux16_2_out_4;  // NOT_Gate not_2, 16 bits wide
  Mux16 mux16_3 (.a(mux16_1_out_4), .b(not_1_out), .sel(nx), .out_4(mux16_3_out_4));
  Mux16 mux16_4 (.a(mux16_2_out_4), .b(not_2_out), .sel(ny), .out_4(mux16_4_out_4));
  assign and_1_out = mux16_3_out_4 & mux16_4_out_4;  // AND_Gate and_1, 16 bits wide
  Add16 add16_1 (.a(mux16_3_out_4), .b(mux16_4_out_4), .out(add16_1_out));
  Mux16 mux16_5 (.a(and_1_out), .b(add16_1_out), .sel(f), .out_4(mux16_5_out_4));
  Mux16 mux16_6 (.a(mux16_5_out_4), .b(not_3_out), .sel(no), .out_4({ng, out[14:0]}));
  assign not_3_out = ~mux16_5_out_4;  // NOT_Gate not_3, 16 bits wide
  Or8Way or8way_1 (
    .in0(out[0]), .in1(out[1]), .in2(out[2]), .in3(out[3]), .in4(out[4]), .in5(out[5]), .in6(out[6]),
    .in7(out[7]), .out(or8way_1_out));
  Or8Way or8way_2 (
    .in0(out[8]), .in1(out[9]), .in2(out[10]), .in3(out[11]), .in4(out[12]), .in5(out[13]), .in6(out[14]),
    .in7(ng), .out(or8way_2_out));
  or or_1 (or_1_out, or8way_1_out, or8way_2_out);
  not not_4 (zr, or_1_out);

  assign out[15] = ng;

  // Notes on the sheet:
  //   Chapter 2: ALU
endmodule

module Main (
);

  HalfAdder halfadder_1 ();  // open: a, b, sum, carry
  FullAdder fulladder_1 ();  // open: a, b, c, sum, carry
  Add16 add16_1 ();  // open: a, b, out
  Inc16 inc16_1 ();  // open: out, in
  ALU alu_1 ();  // open: x, y, out, zr, ng, zx, nx, f, no, zy, ny

  // Notes on the sheet:
  //   Chapter 2: all interfaces
endmodule
