// Logisim project nand2tetris_proj_03.circ as structural Verilog: 9 circuits, main circuit Bit
module Bit (
  input  load,
  input  in,
  input  clock,
  output out
);

  wire multiplexer_1_out;

  Multiplexer #(.enable("false")) multiplexer_1 (.in0(out), .in1(in), .out(multiplexer_1_out), .sel(load));
  D_Flip_Flop d_ff_1 (.clk(clock), .D(multiplexer_1_out), .Q(out));  // open: Qn, preset, en, reset

  // Notes on the sheet:
  //   Chapter 3: 1-Bit Register (Bit)
  //   (DFF)
endmodule

module Register (
  input  load,
  input  [15:0] in,
  input  clock,
  output [15:0] out_4
);

  Bit bit_1 (.clock(clock), .in(in[0]), .load(load), .out(out_4[0]));
  Bit bit_2 (.clock(clock), .in(in[1]), .load(load), .out(out_4[1]));
  Bit bit_3 (.clock(clock), .in(in[2]), .load(load), .out(out_4[2]));
  Bit bit_4 (.clock(clock), .in(in[3]), .load(load), .out(out_4[3]));
  Bit bit_5 (.clock(clock), .in(in[4]), .load(load), .out(out_4[4]));
  Bit bit_6 (.clock(clock), .in(in[5]), .load(load), .out(out_4[5]));
  Bit bit_7 (.clock(clock), .in(in[6]), .load(load), .out(out_4[6]));
  Bit bit_8 (.clock(clock), .in(in[7]), .load(load), .out(out_4[7]));
  Bit bit_9 (.clock(clock), .in(in[8]), .load(load), .out(out_4[8]));
  Bit bit_10 (.clock(clock), .in(in[9]), .load(load), .out(out_4[9]));
  Bit bit_11 (.clock(clock), .in(in[10]), .load(load), .out(out_4[10]));
  Bit bit_12 (.clock(clock), .in(in[11]), .load(load), .out(out_4[11]));
  Bit bit_13 (.clock(clock), .in(in[12]), .load(load), .out(out_4[12]));
  Bit bit_14 (.clock(clock), .in(in[13]), .load(load), .out(out_4[13]));
  Bit bit_15 (.clock(clock), .in(in[14]), .load(load), .out(out_4[14]));
  Bit bit_16 (.clock(clock), .in(in[15]), .load(load), .out(out_4[15]));

  // Notes on the sheet:
  //   Chapter 3: Register (16 bit)
endmodule

module PC (
  input  [15:0] in,
  input  load,
  input  inc,
  input  reset,
  input  clock,
  output [15:0] out
);

  wire or_1_out, or_2_out;
  wire [15:0] adder_1_out, multiplexer_1_out, multiplexer_2_out;

  or or_1 (or_1_out, load, inc);
  Multiplexer #(.width(16), .enable("false")) multiplexer_1 (
    .in0(adder_1_out), .in1(in), .out(multiplexer_1_out), .sel(load));
  or or_2 (or_2_out, or_1_out, reset);
  Multiplexer #(.width(16), .enable("false")) multiplexer_2 (
    .in0(multiplexer_1_out), .in1({16{1'b0}}), .out(multiplexer_2_out), .sel(reset));
  Register register_1 (.in(multiplexer_2_out), .clock(clock), .out_4(out), .load(or_2_out));
  Adder #(.width(16)) adder_1 (.a(out), .b(16'h1), .out(adder_1_out));  // open: cin, cout

  // Notes on the sheet:
  //   Chapter 3: PC (Program Counter)
  //   (add16)
endmodule

module RAM8 (
  input  load,
  input  [15:0] in,
  input  [2:0] address,
  input  clock,
  output [15:0] out
);

  wire dmux8way_1_a, dmux8way_1_b, dmux8way_1_c, dmux8way_1_d, dmux8way_1_e, dmux8way_1_f, dmux8way_1_g,
       dmux8way_1_h;
  wire [15:0] register_1_out_4, register_2_out_4, register_3_out_4, register_4_out_4, register_5_out_4,
       register_6_out_4, register_7_out_4, register_8_out_4;

  DMux8Way dmux8way_1 (
    .in(load), .sel(address), .a(dmux8way_1_a), .b(dmux8way_1_b), .c(dmux8way_1_c), .d(dmux8way_1_d),
    .e(dmux8way_1_e), .f(dmux8way_1_f), .g(dmux8way_1_g), .h(dmux8way_1_h));
  Register register_1 (.in(in), .clock(clock), .out_4(register_1_out_4), .load(dmux8way_1_a));
  Register register_2 (.in(in), .clock(clock), .out_4(register_2_out_4), .load(dmux8way_1_b));
  Register register_3 (.in(in), .clock(clock), .out_4(register_3_out_4), .load(dmux8way_1_c));
  Register register_4 (.in(in), .clock(clock), .out_4(register_4_out_4), .load(dmux8way_1_d));
  Register register_5 (.in(in), .clock(clock), .out_4(register_5_out_4), .load(dmux8way_1_e));
  Register register_6 (.in(in), .clock(clock), .out_4(register_6_out_4), .load(dmux8way_1_f));
  Register register_7 (.in(in), .clock(clock), .out_4(register_7_out_4), .load(dmux8way_1_g));
  Register register_8 (.in(in), .clock(clock), .out_4(register_8_out_4), .load(dmux8way_1_h));
  Mux8Way16 mux8way16_1 (
    .a(register_1_out_4), .b(register_2_out_4), .c(register_3_out_4), .d(register_4_out_4),
    .e(register_5_out_4), .f(register_6_out_4), .g(register_7_out_4), .h(register_8_out_4), .sel(address),
    .out(out));

  // Notes on the sheet:
  //   Chapter 3: RAM8
endmodule

module RAM64 (
  input  load,
  input  [15:0] in,
  input  [5:0] address,
  input  clock,
  output [15:0] out
);

  wire dmux8way_1_a, dmux8way_1_b, dmux8way_1_c, dmux8way_1_d, dmux8way_1_e, dmux8way_1_f, dmux8way_1_g,
       dmux8way_1_h;
  wire [15:0] ram_1_data, ram_2_data, ram_3_data, ram_4_data, ram_5_data, ram_6_data, ram_7_data, ram_8_data;

  DMux8Way dmux8way_1 (
    .in(load), .sel(address[5:3]), .a(dmux8way_1_a), .b(dmux8way_1_b), .c(dmux8way_1_c), .d(dmux8way_1_d),
    .e(dmux8way_1_e), .f(dmux8way_1_f), .g(dmux8way_1_g), .h(dmux8way_1_h));
  RAM #(.addrWidth(3), .dataWidth(16), .bus("separate")) ram_1 (
    .addr(address[2:0]), .din(in), .data(ram_1_data), .str(dmux8way_1_a), .clk(clock));  // open: sel, ld, clr
  RAM #(.addrWidth(3), .dataWidth(16), .bus("separate")) ram_2 (
    .addr(address[2:0]), .din(in), .data(ram_2_data), .str(dmux8way_1_b), .clk(clock));  // open: sel, ld, clr
  RAM #(.addrWidth(3), .dataWidth(16), .bus("separate")) ram_3 (
    .addr(address[2:0]), .din(in), .data(ram_3_data), .str(dmux8way_1_c), .clk(clock));  // open: sel, ld, clr
  RAM #(.addrWidth(3), .dataWidth(16), .bus("separate")) ram_4 (
    .addr(address[2:0]), .din(in), .data(ram_4_data), .str(dmux8way_1_d), .clk(clock));  // open: sel, ld, clr
  RAM #(.addrWidth(3), .dataWidth(16), .bus("separate")) ram_5 (
    .addr(address[2:0]), .din(in), .data(ram_5_data), .str(dmux8way_1_e), .clk(clock));  // open: sel, ld, clr
  RAM #(.addrWidth(3), .dataWidth(16), .bus("separate")) ram_6 (
    .addr(address[2:0]), .din(in), .data(ram_6_data), .str(dmux8way_1_f), .clk(clock));  // open: sel, ld, clr
  RAM #(.addrWidth(3), .dataWidth(16), .bus("separate")) ram_7 (
    .addr(address[2:0]), .din(in), .data(ram_7_data), .str(dmux8way_1_g), .clk(clock));  // open: sel, ld, clr
  RAM #(.addrWidth(3), .dataWidth(16), .bus("separate")) ram_8 (
    .addr(address[2:0]), .din(in), .data(ram_8_data), .str(dmux8way_1_h));  // open: sel, clk, ld, clr
  Mux8Way16 mux8way16_1 (
    .a(ram_1_data), .b(ram_2_data), .c(ram_3_data), .d(ram_4_data), .e(ram_5_data), .f(ram_6_data),
    .g(ram_7_data), .h(ram_8_data), .sel(address[5:3]), .out(out));

  // Notes on the sheet:
  //   Chapter 3: RAM64
  //   (RAM8)
endmodule

module RAM512 (
  input  load,
  input  [15:0] in,
  input  [8:0] address,
  input  clock,
  output [15:0] out
);

  wire dmux8way_1_a, dmux8way_1_b, dmux8way_1_c, dmux8way_1_d, dmux8way_1_e, dmux8way_1_f, dmux8way_1_g,
       dmux8way_1_h;
  wire [15:0] ram_1_data, ram_2_data, ram_3_data, ram_4_data, ram_5_data, ram_6_data, ram_7_data, ram_8_data;

  DMux8Way dmux8way_1 (
    .in(load), .sel(address[8:6]), .a(dmux8way_1_a), .b(dmux8way_1_b), .c(dmux8way_1_c), .d(dmux8way_1_d),
    .e(dmux8way_1_e), .f(dmux8way_1_f), .g(dmux8way_1_g), .h(dmux8way_1_h));
  RAM #(.addrWidth(6), .dataWidth(16), .bus("separate")) ram_1 (
    .addr(address[5:0]), .din(in), .data(ram_1_data), .str(dmux8way_1_a), .clk(clock));  // open: sel, ld, clr
  RAM #(.addrWidth(6), .dataWidth(16), .bus("separate")) ram_2 (
    .addr(address[5:0]), .din(in), .data(ram_2_data), .str(dmux8way_1_b), .clk(clock));  // open: sel, ld, clr
  RAM #(.addrWidth(6), .dataWidth(16), .bus("separate")) ram_3 (
    .addr(address[5:0]), .din(in), .data(ram_3_data), .str(dmux8way_1_c), .clk(clock));  // open: sel, ld, clr
  RAM #(.addrWidth(6), .dataWidth(16), .bus("separate")) ram_4 (
    .addr(address[5:0]), .din(in), .data(ram_4_data), .str(dmux8way_1_d), .clk(clock));  // open: sel, ld, clr
  RAM #(.addrWidth(6), .dataWidth(16), .bus("separate")) ram_5 (
    .addr(address[5:0]), .din(in), .data(ram_5_data), .str(dmux8way_1_e), .clk(clock));  // open: sel, ld, clr
  RAM #(.addrWidth(6), .dataWidth(16), .bus("separate")) ram_6 (
    .addr(address[5:0]), .din(in), .data(ram_6_data), .str(dmux8way_1_f), .clk(clock));  // open: sel, ld, clr
  RAM #(.addrWidth(6), .dataWidth(16), .bus("separate")) ram_7 (
    .addr(address[5:0]), .din(in), .data(ram_7_data), .str(dmux8way_1_g), .clk(clock));  // open: sel, ld, clr
  RAM #(.addrWidth(6), .dataWidth(16), .bus("separate")) ram_8 (
    .addr(address[5:0]), .din(in), .data(ram_8_data), .str(dmux8way_1_h));  // open: sel, clk, ld, clr
  Mux8Way16 mux8way16_1 (
    .a(ram_1_data), .b(ram_2_data), .c(ram_3_data), .d(ram_4_data), .e(ram_5_data), .f(ram_6_data),
    .g(ram_7_data), .h(ram_8_data), .sel(address[8:6]), .out(out));

  // Notes on the sheet:
  //   Chapter 3: RAM512
  //   (RAM64)
endmodule

module RAM4K (
  input  load,
  input  [15:0] in,
  input  [11:0] address,
  input  clock,
  output [15:0] out
);

  wire dmux8way_1_a, dmux8way_1_b, dmux8way_1_c, dmux8way_1_d, dmux8way_1_e, dmux8way_1_f, dmux8way_1_g,
       dmux8way_1_h;
  wire [15:0] ram_1_data, ram_2_data, ram_3_data, ram_4_data, ram_5_data, ram_6_data, ram_7_data, ram_8_data;

  DMux8Way dmux8way_1 (
    .in(load), .sel(address[11:9]), .a(dmux8way_1_a), .b(dmux8way_1_b), .c(dmux8way_1_c), .d(dmux8way_1_d),
    .e(dmux8way_1_e), .f(dmux8way_1_f), .g(dmux8way_1_g), .h(dmux8way_1_h));
  RAM #(.addrWidth(9), .dataWidth(16), .bus("separate")) ram_1 (
    .addr(address[8:0]), .din(in), .data(ram_1_data), .str(dmux8way_1_a), .clk(clock));  // open: sel, ld, clr
  RAM #(.addrWidth(9), .dataWidth(16), .bus("separate")) ram_2 (
    .addr(address[8:0]), .din(in), .data(ram_2_data), .str(dmux8way_1_b), .clk(clock));  // open: sel, ld, clr
  RAM #(.addrWidth(9), .dataWidth(16), .bus("separate")) ram_3 (
    .addr(address[8:0]), .din(in), .data(ram_3_data), .str(dmux8way_1_c), .clk(clock));  // open: sel, ld, clr
  RAM #(.addrWidth(9), .dataWidth(16), .bus("separate")) ram_4 (
    .addr(address[8:0]), .din(in), .data(ram_4_data), .str(dmux8way_1_d), .clk(clock));  // open: sel, ld, clr
  RAM #(.addrWidth(9), .dataWidth(16), .bus("separate")) ram_5 (
    .addr(address[8:0]), .din(in), .data(ram_5_data), .str(dmux8way_1_e), .clk(clock));  // open: sel, ld, clr
  RAM #(.addrWidth(9), .dataWidth(16), .bus("separate")) ram_6 (
    .addr(address[8:0]), .din(in), .data(ram_6_data), .str(dmux8way_1_f), .clk(clock));  // open: sel, ld, clr
  RAM #(.addrWidth(9), .dataWidth(16), .bus("separate")) ram_7 (
    .addr(address[8:0]), .din(in), .data(ram_7_data), .str(dmux8way_1_g), .clk(clock));  // open: sel, ld, clr
  RAM #(.addrWidth(9), .dataWidth(16), .bus("separate")) ram_8 (
    .addr(address[8:0]), .din(in), .data(ram_8_data), .str(dmux8way_1_h));  // open: sel, clk, ld, clr
  Mux8Way16 mux8way16_1 (
    .a(ram_1_data), .b(ram_2_data), .c(ram_3_data), .d(ram_4_data), .e(ram_5_data), .f(ram_6_data),
    .g(ram_7_data), .h(ram_8_data), .sel(address[11:9]), .out(out));

  // Notes on the sheet:
  //   Chapter 3: RAM4K
  //   (RAM512)
endmodule

module RAM16K (
  input  load,
  input  [15:0] in,
  input  [13:0] address,
  input  clock,
  output [15:0] out
);

  wire dmux4way_1_a, dmux4way_1_b, dmux4way_1_c, dmux4way_1_d;
  wire [15:0] ram_1_data, ram_2_data, ram_3_data, ram_4_data, undriven;

  DMux4Way dmux4way_1 (
    .in(load), .a(dmux4way_1_a), .b(dmux4way_1_b), .c(dmux4way_1_c), .d(dmux4way_1_d), .in_2(address[13:12]));
  RAM #(.addrWidth(12), .dataWidth(16), .bus("separate")) ram_1 (
    .addr(address[11:0]), .din(undriven), .data(ram_1_data), .str(dmux4way_1_a), .clk(clock));  // open: sel, ld, clr
  RAM #(.addrWidth(12), .dataWidth(16), .bus("separate")) ram_2 (
    .addr(address[11:0]), .din(undriven), .data(ram_2_data), .str(dmux4way_1_b), .clk(clock));  // open: sel, ld, clr
  RAM #(.addrWidth(12), .dataWidth(16), .bus("separate")) ram_3 (
    .addr(address[11:0]), .din(undriven), .data(ram_3_data), .str(dmux4way_1_c), .clk(clock));  // open: sel, ld, clr
  RAM #(.addrWidth(12), .dataWidth(16), .bus("separate")) ram_4 (
    .addr(address[11:0]), .din(undriven), .data(ram_4_data), .str(dmux4way_1_d), .clk(clock));  // open: sel, ld, clr
  Mux4Way16 mux4way16_1 (
    .a(ram_1_data), .b(ram_2_data), .c(ram_3_data), .d(ram_4_data), .out(out), .sel(address[13:12]));

  // Notes on the sheet:
  //   Chapter 3: RAM16K
  //   (RAM4K)
endmodule

module Main (
);

  Bit bit_1 ();  // open: clock, in, load, out
  Register register_1 ();  // open: in, clock, out_4, load
  PC pc_1 ();  // open: in, load, inc, reset, clock, out
  RAM8 ram8_1 ();  // open: in, load, address, out, clock
  RAM64 ram64_1 ();  // open: load, in, address, clock, out
  RAM512 ram512_1 ();  // open: load, in, address, clock, out
  RAM4K ram4k_1 ();  // open: load, in, address, clock, out
  RAM16K ram16k_1 ();  // open: load, in, address, clock, out

  // Notes on the sheet:
  //   Chapter 3: all interfaces
endmodule
