// Logisim project nand2tetris_proj_05.circ as structural Verilog: 8 circuits, main circuit Decoder
module Decoder (
  input  [15:0] in,
  output i,
  output a,
  output c1,
  output c2,
  output c3,
  output c4,
  output c5,
  output c6,
  output d1,
  output d2,
  output d3,
  output j1,
  output j2,
  output j3
);

  Multiplexer #(.enable("false")) multiplexer_1 (.in0(1'b0), .in1(in[12]), .out(a), .sel(in[15]));
  Multiplexer #(.enable("false")) multiplexer_2 (.in0(1'b0), .in1(in[11]), .out(c1), .sel(in[15]));
  Multiplexer #(.enable("false")) multiplexer_3 (.in0(1'b0), .in1(in[10]), .out(c2), .sel(in[15]));
  Multiplexer #(.enable("false")) multiplexer_4 (.in0(1'b0), .in1(in[9]), .out(c3), .sel(in[15]));
  Multiplexer #(.enable("false")) multiplexer_5 (.in0(1'b0), .in1(in[8]), .out(c4), .sel(in[15]));
  Multiplexer #(.enable("false")) multiplexer_6 (.in0(1'b0), .in1(in[7]), .out(c5), .sel(in[15]));
  Multiplexer #(.enable("false")) multiplexer_7 (.in0(1'b0), .in1(in[6]), .out(c6), .sel(in[15]));
  Multiplexer #(.enable("false")) multiplexer_8 (.in0(1'b0), .in1(in[5]), .out(d1), .sel(in[15]));
  Multiplexer #(.enable("false")) multiplexer_9 (.in0(1'b0), .in1(in[4]), .out(d2), .sel(in[15]));
  Multiplexer #(.enable("false")) multiplexer_10 (.in0(1'b0), .in1(in[3]), .out(d3), .sel(in[15]));
  Multiplexer #(.enable("false")) multiplexer_11 (.in0(1'b0), .in1(in[2]), .out(j1), .sel(in[15]));
  Multiplexer #(.enable("false")) multiplexer_12 (.in0(1'b0), .in1(in[1]), .out(j2), .sel(in[15]));
  Multiplexer #(.enable("false")) multiplexer_13 (.in0(1'b0), .in1(in[0]), .out(j3), .sel(in[15]));

  assign i = in[15];

  // Notes on the sheet:
  //   Chapter 5: Decoder
  //   This is an extra chip to decode the instructions for the CPU control inputs.
endmodule

module CPU (
  input  [15:0] instruction,
  input  [15:0] inM,
  input  reset,
  input  in_4,
  output [15:0] outM,
  output writeM,
  output [14:0] addressM,
  output [14:0] pc
);

  wire alu_1_ng, alu_1_zr, and_1_out, and_2_out, and_3_out, decoder_1_a, decoder_1_c1, decoder_1_c2,
       decoder_1_c3, decoder_1_c4, decoder_1_c5, decoder_1_c6, decoder_1_d1, decoder_1_d2, decoder_1_i,
       decoder_1_j1, decoder_1_j2, decoder_1_j3, not_1_out, not_2_out, not_3_out, not_4_out, not_5_out,
       or_1_out, or_2_out, pc_1_p3;
  wire [15:0] mux16_1_out_4, mux16_2_out_4, register_2_p4;
  wire [15:15] pc_1_p6, register_1_p4;

  Decoder decoder_1 (
    .in(instruction), .i(decoder_1_i), .a(decoder_1_a), .c1(decoder_1_c1), .c2(decoder_1_c2),
    .c3(decoder_1_c3), .c4(decoder_1_c4), .c5(decoder_1_c5), .c6(decoder_1_c6), .d1(decoder_1_d1),
    .d2(decoder_1_d2), .d3(writeM), .j1(decoder_1_j1), .j2(decoder_1_j2), .j3(decoder_1_j3));
  or or_1 (or_1_out, not_2_out, not_1_out);
  not not_1 (not_1_out, decoder_1_d1);
  not not_2 (not_2_out, decoder_1_i);
  Mux16 mux16_1 (.a(outM), .b(instruction), .sel(or_1_out), .out_4(mux16_1_out_4));
  or or_2 (or_2_out, not_2_out, decoder_1_d1);
  // Register register_1: pin names not known; wires that end beside it: mux16_1_out_4, or_2_out, in_4, {register_1_p4[15], addressM}
  // Register register_2: pin names not known; wires that end beside it: outM, decoder_1_d2, in_4, register_2_p4
  Mux16 mux16_2 (.a({register_1_p4[15], addressM}), .b(inM), .sel(decoder_1_a), .out_4(mux16_2_out_4));
  not not_3 (not_3_out, pc_1_p3);
  // PC pc_1: pin names not known; wires that end beside it: {register_1_p4[15], addressM}, not_3_out, pc_1_p3, in_4, reset, {pc_1_p6[15], pc}
  and and_1 (and_1_out, decoder_1_j1, not_4_out, alu_1_ng);
  and and_2 (and_2_out, decoder_1_j2, alu_1_zr, not_5_out);
  and and_3 (and_3_out, decoder_1_j3, not_4_out, not_5_out);
  not not_4 (not_4_out, alu_1_zr);
  not not_5 (not_5_out, alu_1_ng);
  ALU alu_1 (
    .x(register_2_p4), .y(mux16_2_out_4), .out(outM), .zr(alu_1_zr), .ng(alu_1_ng), .zx(decoder_1_c1),
    .nx(decoder_1_c2), .f(decoder_1_c5), .no(decoder_1_c6), .zy(decoder_1_c3), .ny(decoder_1_c4));
  or or_3 (pc_1_p3, and_1_out, and_2_out, and_3_out);

  // Notes on the sheet:
  //   Chapter 5: CPU
  //   sel: ~i + ~d1
  //   ~i + ~d1
  //   A
  //   ~i + d1
  //   ~i + d1
  //   d2
  //   D
  //   sel: a
  //   j1 ~zr ng
  //   j2 zr ~ng
  //   j3 ~zr ~ng
  //   zr
  //   ~zr
  //   ng
  //   ~ng
  //   jump
  //   d3
endmodule

module Screen (
  input  [12:0] address,
  input  [15:0] in,
  input  load,
  input  clock,
  output [15:0] out
);

  RAM #(.addrWidth(13), .dataWidth(16), .bus("separate")) ram_1 (
    .addr(address), .din(in), .data(out), .str(load), .clk(clock));  // open: sel, ld, clr

  // Notes on the sheet:
  //   Chapter 5: Screen
  //   RAM8K
endmodule

module Keyboard (
  output [15:0] out
);


  assign out = {16{1'b1}};

  // Notes on the sheet:
  //   Chapter 5: Keyboard
  //   this constant represents a random input from the keyboard
endmodule

module Memory (
  input  load,
  input  [15:0] in,
  input  clock,
  input  [14:0] address,
  output [15:0] out
);

  wire demux_1_a, demux_1_b;
  wire [15:0] keyboard_1_out, mux16_1_out_4, ram16k_1_p5, ram16k_1_p6;

  Demux demux_1 (.in(load), .a(demux_1_a), .b(demux_1_b), .sel(address[14]));
  // RAM16K ram16k_1: pin names not known; wires that end beside it: in, address[13:0], demux_1_a, clock, ram16k_1_p5, ram16k_1_p6
  Screen screen_1 (.address(address[12:0]), .in(in), .load(demux_1_b), .out(ram16k_1_p6), .clock(clock));
  Keyboard keyboard_1 (.out(keyboard_1_out));
  Mux16 mux16_1 (.a(ram16k_1_p6), .b(keyboard_1_out), .sel(address[13]), .out_4(mux16_1_out_4));
  Mux16 mux16_2 (.a(ram16k_1_p5), .b(mux16_1_out_4), .sel(address[14]), .out_4(out));

  // Notes on the sheet:
  //   Chapter 5: Memory
endmodule

module ROM32K (
  input  [14:0] address,
  output [15:0] out
);

  ROM #(.addrWidth(15), .dataWidth(16)) rom_1 (.addr(address), .data(out));  // open: sel

  // Notes on the sheet:
  //   Chapter 5: ROM32K (Instruction Memory)
endmodule

module Computer (
  input  reset,
  input  clock
);

  wire cpu_1_writem;
  wire [14:0] cpu_1_addressm, cpu_1_pc;
  wire [15:0] cpu_1_outm, memory_1_out, rom32k_1_out;

  ROM32K rom32k_1 (.address(cpu_1_pc), .out(rom32k_1_out));
  CPU cpu_1 (
    .instruction(rom32k_1_out), .inM(memory_1_out), .reset(reset), .in_4(clock), .outM(cpu_1_outm),
    .writeM(cpu_1_writem), .addressM(cpu_1_addressm), .pc(cpu_1_pc));
  Memory memory_1 (.load(cpu_1_writem), .in(cpu_1_outm), .clock(clock), .address(cpu_1_addressm), .out(memory_1_out));

  // Notes on the sheet:
  //   Chapter 5: Computer
  //   (instruction memory)
  //   (data memory)
endmodule

module Main (
);

  Decoder decoder_1 ();  // open: in, i, a, c1, c2, c3, c4, c5, c6, d1, d2, d3, j1, j2, j3
  CPU cpu_1 ();  // open: instruction, inM, reset, in_4, outM, writeM, addressM, pc
  Screen screen_1 ();  // open: address, in, load, out, clock
  Keyboard keyboard_1 ();  // open: out
  Memory memory_1 ();  // open: load, in, clock, address, out
  ROM32K rom32k_1 ();  // open: address, out
  Computer computer_1 ();  // open: reset, clock

  // Notes on the sheet:
  //   Chapter 5: all interfaces
endmodule
